# Fritzing sketch rotary-dial (saved by Fritzing 0.8.5b)
breadboards: 1

parts:
  J2 = male pin header, 5 pins [form="♂ (male)"]
  R4 = Resistor [tolerance=±5% resistance=10k package=THT]
  C2 = Electrolytic Capacitor [capacitance=100µF package="100 mil [THT, electrolytic]"]
  R5 = Resistor [tolerance=±5% resistance=220 package=THT]
  U3 = mystery part, 5 pins [chip_label="Rotary Dial"]
  R6 = Resistor [tolerance=±5% resistance=220 package=THT]

nets:
  N1: J2.pin1, C2.-, R5.Pin_1, R6.Pin_1
  N2: J2.pin2, U3.pin2, U3.pin5
  N3: J2.pin3, U3.pin3, R6.Pin_0
  N4: J2.pin4, R4.Pin_1, C2.+
  N5: J2.pin5, U3.pin4
  N6: R4.Pin_0, U3.pin1
